# Fritzing sketch cloudlamp (saved by Fritzing 0.9.3b)
breadboards: 1

parts:
  Bauteil1 = Arduino Nano (Rev3.0) (ICSP)
  Bauteil2 = Arduino Nano (Rev3.0) (ICSP)
  Power_plug1 = Power plug
  Bauteil3 = Breakout Board for Electret Microphone
  RGB_SMD_LED1 = SMD RGB LED (WS2812) [package=5050]
  R1 = Resistor [tolerance=±5% resistance=2.2k package=THT]
  R2 = Resistor [tolerance=±5% resistance=2.2k package=THT]
  IR1 = TSOP312.., 314.. [package=THT]

nets:
  N1: Bauteil1.D11/MOSI, IR1.Data
  VIN: Bauteil1.VIN, Power_plug1.VCC, RGB_SMD_LED1.VDD
  GND: Bauteil1.GND, Power_plug1.GND, Bauteil3.GND, RGB_SMD_LED1.VSS, IR1.GND
  N2: Bauteil1.5V, R1.Pin_1, R2.Pin_0, IR1.Vs
  N3: Bauteil1.A5, Bauteil2.A5, R2.Pin_1
  N4: Bauteil1.A4, Bauteil2.A4, R1.Pin_0
  N5: Bauteil2.D6, RGB_SMD_LED1.DIn
  5V: Bauteil2.5V, Bauteil3.VCC
  N6: Bauteil2.A0, Bauteil3.AUD

notes:
  12 V
  IR_Receiver.ino
  ThunderCloud.ino
